# Fritzing sketch esquema fritzing despertadorSolar (saved by Fritzing 1.0.3b)
breadboards: 1

parts:
  A1 = Arduino UNO R4 WiFi
  LCD2004-I2C1 = LCD2004-I2C

nets:
  N1: A1.Pin_11, LCD2004-I2C1.VCC
  N2: A1.Pin_16, LCD2004-I2C1.SDA
  N3: A1.Pin_17, LCD2004-I2C1.SCL

custom parts:
  Arduino UNO R4 WiFi: The Arduino UNO R4 WiFi merges the RA4M1 microprocessor from Renesas with the ESP32-S3 from Espressif, creating an all-in-one tool for makers with enhanced processing power and a diverse array of new peripherals.
  LCD2004-I2C: A standard character display with 4x20 characters. Comes in many colors with LCM2004 IIC attached.
